# Fritzing sketch TP1-3 (saved by Fritzing 0.9.3b)
breadboards: 1

parts:
  Part1 = Arduino Uno (Rev3)
  U1 = 7-SEGMENT-DISPLAY [package=7-segment-display]
  R1 = Resistor [tolerance=±5% resistance=220 package=THT]

nets:
  N1: Part1.D8, U1.E
  N2: Part1.D9_PWM, U1.B
  N3: Part1.D2, U1.G2
  N4: Part1.D3_PWM, U1.A
  N5: Part1.D4, U1.DP
  N6: Part1.D5_PWM, U1.G1
  N7: Part1.D6_PWM, U1.D
  N8: Part1.D7, U1.G
  N9: Part1.GND, R1.Pin_1
  N10: U1.C, U1.F, R1.Pin_0
