# Fritzing sketch TP3-1 (saved by Fritzing 0.9.3b)
breadboards: 1

parts:
  Part1 = Arduino Uno (Rev3)
  R1 = Resistor [tolerance=±5% resistance=220 package=THT]
  LED1 = LED - 5mm [color="Red (633nm)" package="5 mm [THT]"]
  S1 = Pushbutton [package="[THT]"]
  R2 = Resistor [tolerance=±5% resistance=220 package=THT]

nets:
  N1: Part1.D8, S1.Pin_3, S1.Pin_4, R2.Pin_0
  N2: Part1.D13/SCK, LED1.anode
  N3: Part1.5V, S1.Pin_1, S1.Pin_2
  N4: Part1.GND, R1.Pin_1, R2.Pin_1
  N5: R1.Pin_0, LED1.cathode
