# Fritzing sketch TP3-2 (saved by Fritzing 0.9.3b)
breadboards: 1

parts:
  Part1 = Arduino Uno (Rev3)
  R1 = Resistor [tolerance=±5% resistance=220 package=THT]
  LED1 = LED - 5mm [color="Red (633nm)" package="5 mm [THT]"]
  S1 = Pushbutton [package="[THT]"]
  R2 = Resistor [tolerance=±5% resistance=220 package=THT]
  S2 = SWITCH-MOMENTARY-2 [package=tactile_switch_tall]
  S3 = SWITCH-MOMENTARY-2 [package=tactile_switch_tall]
  S4 = SWITCH-MOMENTARY-2 [package=tactile_switch_tall]
  S5 = SWITCH-MOMENTARY-2 [package=tactile_switch_tall]  # not connected
  S6 = SWITCH-MOMENTARY-2 [package=tactile_switch_tall]  # not connected
  S7 = SWITCH-MOMENTARY-2 [package=tactile_switch_tall]  # not connected
  S8 = SWITCH-MOMENTARY-2 [package=tactile_switch_tall]  # not connected
  S9 = SWITCH-MOMENTARY-2 [package=tactile_switch_tall]  # not connected
  S10 = SWITCH-MOMENTARY-2 [package=tactile_switch_tall]  # not connected
  S11 = SWITCH-MOMENTARY-2 [package=tactile_switch_tall]  # not connected
  S12 = SWITCH-MOMENTARY-2 [package=tactile_switch_tall]  # not connected
  S13 = SWITCH-MOMENTARY-2 [package=tactile_switch_tall]  # not connected
  S14 = SWITCH-MOMENTARY-2 [package=tactile_switch_tall]  # not connected
  S15 = SWITCH-MOMENTARY-2 [package=tactile_switch_tall]  # not connected
  S16 = SWITCH-MOMENTARY-2 [package=tactile_switch_tall]  # not connected
  S17 = SWITCH-MOMENTARY-2 [package=tactile_switch_tall]  # not connected

nets:
  N1: Part1.D8, S1.Pin_3, S1.Pin_4, R2.Pin_0
  N2: Part1.D13/SCK, LED1.anode
  N3: Part1.5V, S1.Pin_1, S1.Pin_2
  N4: Part1.GND, R1.Pin_1, R2.Pin_1
  N5: R1.Pin_0, LED1.cathode
  N6: S2.2, S3.2, S4.2
