# Fritzing sketch TP3-3 (saved by Fritzing 0.9.3b)
breadboards: 1

parts:
  Part1 = Arduino Uno (Rev3)
  LCD1 = LCD screen
  R1 = Trimmer Potentiometer [maximum_resistance=10kΩ package=THT]
  R2 = Resistor [tolerance=±5% resistance=10k package=THT]
  Matrix_keypad1 = KEYPAD 4x4

nets:
  N1: Part1.A0, Matrix_keypad1.col1
  N2: Part1.A1, Matrix_keypad1.col2
  N3: Part1.D8, Matrix_keypad1.row2
  N4: Part1.D9_PWM, Matrix_keypad1.row1
  N5: Part1.D10_PWM/SS, Matrix_keypad1.col4
  N6: Part1.D11_PWM/MOSI, LCD1.E
  N7: Part1.D12/MISO, LCD1.RS
  N8: Part1.D13/SCK, Matrix_keypad1.col3
  N9: Part1.D2, LCD1.DB7
  N10: Part1.D3_PWM, LCD1.DB6
  N11: Part1.D4, LCD1.DB5
  N12: Part1.D5_PWM, LCD1.DB4
  N13: Part1.D6_PWM, Matrix_keypad1.row4
  N14: Part1.D7, Matrix_keypad1.row3
  5V: Part1.5V, LCD1.VDD, R1.leg2, R2.Pin_0
  GND: Part1.GND, LCD1.VSS, LCD1.R/W, LCD1.LED-, R1.leg1
  N15: LCD1.V0, R1.wiper
  N16: LCD1.LED+, R2.Pin_1

custom parts:
  KEYPAD 4x4: Matrix keypad 16 buttons, 4 rows x 4 columns
