# Fritzing sketch TP4-2 (saved by Fritzing 0.9.3b)
breadboards: 1

parts:
  Part1 = Arduino Uno (Rev3)
  R1 = Resistor [tolerance=±5% resistance=220 package=THT]
  LED1 = LED - 5mm [color="Red (633nm)" package="5 mm [THT]"]
  IR1 = TSOP312.., 314.. [package=THT]

nets:
  N1: Part1.D8, IR1.GND
  N2: Part1.D13/SCK, LED1.anode
  N3: Part1.5V, IR1.Data
  N4: Part1.GND, R1.Pin_1, IR1.Vs
  N5: R1.Pin_0, LED1.cathode
