# Fritzing sketch TP4-3 (saved by Fritzing 0.9.3b)
breadboards: 1

parts:
  Part1 = Arduino Uno (Rev3)
  R1 = Resistor [tolerance=±5% resistance=220 package=THT]
  LED1 = RGB LED (com. cathode, rgb) [package="5 mm [THT]"]
  IR1 = TSOP312.., 314.. [package=THT]

nets:
  N1: Part1.D8, IR1.GND
  N2: Part1.D9_PWM, LED1.blue_anode
  N3: Part1.D10_PWM/SS, LED1.green_anode
  N4: Part1.D11_PWM/MOSI, LED1.red_anode
  N5: Part1.5V, IR1.Data
  N6: Part1.GND, R1.Pin_1, IR1.Vs
  N7: R1.Pin_0, LED1.common_cathode
